// Logisim project 01-demp_lab.circ as structural Verilog
module _01_demp_work (
);

  wire nand_1_out, undriven;

  nand nand_1 (nand_1_out, undriven, undriven);
endmodule
