// Logisim project vivek-demp-lab-worksheet-2-final.circ as structural Verilog
module _01 (
  input  in_1,
  input  in_2,
  output out_3,
  output out_4
);

  and and_1 (out_4, in_1, in_2);
  xor xor_1 (out_3, in_1, in_2);

  // Notes on the sheet:
  //   NAME : VIVEK KUMAR
  //   BITS ID: 202419TW021
endmodule

module _02 (
  input  in_1,
  input  in_2,
  output out_3,
  output out_4
);

  wire nand_1_out, nand_2_out, nand_3_out;

  nand nand_1 (nand_1_out, in_1, in_2);
  nand nand_2 (nand_2_out, in_1, nand_1_out);
  nand nand_3 (nand_3_out, nand_1_out, in_2);
  nand nand_4 (out_3, nand_2_out, nand_3_out);
  not nand_5 (out_4, nand_1_out);  // NAND_Gate
endmodule

module _03 (
  input  in_1,
  input  in_2,
  input  in_3,
  output out_4,
  output out_5
);

  wire and_1_out, and_2_out, xor_1_out;

  and and_1 (and_1_out, in_1, in_2);
  xor xor_1 (xor_1_out, in_1, in_2);
  xor xor_2 (out_4, xor_1_out, in_3);
  and and_2 (and_2_out, xor_1_out, in_3);
  or or_1 (out_5, and_2_out, and_1_out);
endmodule

module _04 (
  input  A,
  input  B,
  input  C,
  output out_4,
  output out_5
);

  wire nand_1_out, nand_2_out, nand_3_out, nand_4_out, nand_5_out, nand_6_out, nand_7_out;

  nand nand_1 (nand_1_out, A, B);
  nand nand_2 (nand_2_out, A, nand_1_out);
  nand nand_3 (nand_3_out, nand_1_out, B);
  nand nand_4 (nand_4_out, nand_2_out, nand_3_out);
  nand nand_5 (nand_5_out, nand_4_out, C);
  nand nand_6 (nand_6_out, nand_4_out, nand_5_out);
  nand nand_7 (nand_7_out, nand_5_out, C);
  nand nand_8 (out_4, nand_6_out, nand_7_out);
  nand nand_9 (out_5, nand_5_out, nand_1_out);
endmodule

module _06 (
  input  A,
  input  B,
  output X,
  output Y
);

  wire not_1_out;

  xor xor_1 (X, A, B);
  not not_1 (not_1_out, A);
  and and_1 (Y, not_1_out, B);
endmodule

module _07 (
  input  in_1,
  input  in_2,
  output out_3,
  output out_4
);

  wire nand_1_out, nand_2_out, nand_3_out;

  nand nand_1 (nand_1_out, in_1, in_2);
  nand nand_2 (nand_2_out, in_1, nand_1_out);
  nand nand_3 (nand_3_out, nand_1_out, in_2);
  nand nand_4 (out_3, nand_2_out, nand_3_out);
  nand nand_5 (out_4, nand_3_out, nand_3_out);
endmodule

module _08 (
  input  in_1,
  input  in_2,
  input  in_3,
  output out_4,
  output out_5
);

  wire and_1_out, and_2_out, not_1_out, not_2_out, xor_1_out;

  xor xor_1 (xor_1_out, in_1, in_2);
  not not_1 (not_1_out, in_1);
  xor xor_2 (out_4, xor_1_out, in_3);
  and and_1 (and_1_out, not_1_out, in_2);
  not not_2 (not_2_out, xor_1_out);
  and and_2 (and_2_out, not_2_out, in_3);
  or or_1 (out_5, and_2_out, and_1_out);
endmodule

module _09 (
  input  in_1,
  input  in_2,
  input  in_3,
  output out_4,
  output out_5
);

  wire nand_1_out, nand_2_out, nand_3_out, nand_4_out, nand_5_out, nand_6_out, nand_7_out;

  nand nand_1 (nand_1_out, in_1, in_2);
  nand nand_2 (nand_2_out, in_1, nand_1_out);
  nand nand_3 (nand_3_out, nand_1_out, in_2);
  nand nand_4 (nand_4_out, nand_2_out, nand_3_out);
  nand nand_5 (nand_5_out, nand_4_out, in_3);
  nand nand_6 (nand_6_out, nand_4_out, nand_5_out);
  nand nand_7 (nand_7_out, nand_5_out, in_3);
  nand nand_8 (out_4, nand_6_out, nand_7_out);
  nand nand_9 (out_5, nand_7_out, nand_3_out);
endmodule

module _10 (
  input  B3,
  input  B2,
  input  B1,
  input  B0,
  output G3,
  output G2,
  output G1,
  output G0
);

  xor xor_1 (G3, B3, B2);
  xor xor_2 (G2, B2, B1);
  xor xor_3 (G1, B1, B0);

  assign G0 = B0;
endmodule

module _11 (
  input  B0,
  input  B1,
  input  B2,
  input  B3,
  output G0,
  output G1,
  output G2,
  output G3
);

  wire nand_1_out, nand_2_out, nand_3_out, nand_4_out, nand_5_out, nand_6_out, nand_7_out, nand_8_out,
       nand_9_out;

  nand nand_1 (nand_1_out, B0, B1);
  nand nand_2 (nand_2_out, B1, B2);
  nand nand_3 (nand_3_out, B2, B3);
  nand nand_4 (nand_4_out, B0, nand_1_out);
  nand nand_5 (nand_5_out, nand_1_out, B1);
  nand nand_6 (nand_6_out, B1, nand_2_out);
  nand nand_7 (nand_7_out, nand_2_out, B2);
  nand nand_8 (nand_8_out, B2, nand_3_out);
  nand nand_9 (nand_9_out, nand_3_out, B3);
  nand nand_10 (G1, nand_4_out, nand_5_out);
  nand nand_11 (G2, nand_6_out, nand_7_out);
  nand nand_12 (G3, nand_8_out, nand_9_out);

  assign G0 = B0;
endmodule

// G0
module _12 (
  input  G0,
  input  G1,
  input  G3,
  input  G3_2,
  output B0,
  output B1,
  output B2,
  output B3
);

  xor xor_1 (B1, G0, G1);
  xor xor_2 (B2, B1, G3);
  xor xor_3 (B3, B2, G3_2);

  assign B0 = G0;
endmodule

module _13 (
  input  G0,
  input  G1,
  input  G2,
  input  G3,
  output B0,
  output B1,
  output B2,
  output B3
);

  wire nand_1_out, nand_2_out, nand_3_out, nand_5_out, nand_6_out, nand_7_out, nand_9_out, nand_10_out,
       nand_11_out;

  nand nand_1 (nand_1_out, G0, G1);
  nand nand_2 (nand_2_out, G0, nand_1_out);
  nand nand_3 (nand_3_out, nand_1_out, G1);
  nand nand_4 (B1, nand_2_out, nand_3_out);
  nand nand_5 (nand_5_out, B1, G2);
  nand nand_6 (nand_6_out, B1, nand_5_out);
  nand nand_7 (nand_7_out, nand_5_out, G2);
  nand nand_8 (B2, nand_6_out, nand_7_out);
  nand nand_9 (nand_9_out, B2, G3);
  nand nand_10 (nand_10_out, B2, nand_9_out);
  nand nand_11 (nand_11_out, nand_9_out, G3);
  nand nand_12 (B3, nand_10_out, nand_11_out);

  assign B0 = G0;
endmodule
