// Logisim project demp_lab_3.circ as structural Verilog: 5 circuits, main circuit 01
module _01 (
  input  A,
  input  B,
  input  I0,
  input  I1,
  input  I2,
  input  I3,
  output X
);

  wire nand_1_out, nand_2_out, nand_3_out, nand_4_out, nand_5_out, nand_6_out;

  nand nand_1 (nand_1_out, A, A);
  nand nand_2 (nand_2_out, B, B);
  nand nand_3 (nand_3_out, nand_2_out, I0, nand_1_out);
  nand nand_4 (nand_4_out, B, nand_1_out, I1);
  nand nand_5 (nand_5_out, nand_2_out, A, I2);
  nand nand_6 (nand_6_out, B, A, I3);
  nand nand_7 (X, nand_3_out, nand_4_out, nand_5_out, nand_6_out);
endmodule

module _02 (
  input  A,
  input  B,
  input  E,
  output Y0,
  output Y1,
  output Y2,
  output Y3
);

  wire nand_1_out, nand_2_out, nand_3_out;

  nand nand_1 (nand_1_out, A, A);
  nand nand_2 (nand_2_out, B, B);
  nand nand_3 (nand_3_out, E, E);
  nand nand_4 (Y0, nand_1_out, nand_2_out, nand_3_out);
  nand nand_5 (Y1, nand_1_out, B, nand_3_out);
  nand nand_6 (Y2, A, nand_2_out, nand_3_out);
  nand nand_7 (Y3, A, B, nand_3_out);
endmodule

module _03 (
  input  in_1,
  input  in_2,
  input  in_3,
  input  in_4,
  input  in_5,
  input  in_6,
  input  in_7,
  input  in_8,
  input  in_9,
  input  in_10,
  input  in_11,
  input  in_12,
  output out_13,
  output out_14
);

  wire and_1_out, and_2_out, and_3_out, and_4_out, and_5_out, and_6_out, and_7_out, and_8_out, not_1_out,
       not_2_out, not_3_out, not_4_out, not_5_out, not_6_out, not_7_out;

  not not_1 (not_1_out, in_9);
  not not_2 (not_2_out, in_10);
  not not_3 (not_3_out, in_11);
  not not_4 (not_4_out, not_1_out);
  not not_5 (not_5_out, not_2_out);
  not not_6 (not_6_out, not_3_out);
  not not_7 (not_7_out, in_12);
  and and_1 (and_1_out, not_7_out, not_6_out, not_3_out, not_4_out, in_1);
  and and_2 (and_2_out, not_7_out, not_6_out, not_3_out, not_4_out, in_2);
  and and_3 (and_3_out, not_7_out, not_2_out, not_5_out, not_4_out, in_3);
  and and_4 (and_4_out, not_7_out, not_2_out, not_5_out, not_4_out, in_4);
  nand nand_1 (out_13, and_1_out, and_2_out, and_3_out, and_4_out, and_5_out, and_6_out, and_7_out, and_8_out);
  not not_8 (out_14, out_13);
  and and_5 (and_5_out, not_7_out, not_6_out, not_2_out, not_1_out, in_5);
  and and_6 (and_6_out, not_7_out, not_3_out, not_5_out, not_1_out, in_6);
  and and_7 (and_7_out, not_7_out, not_6_out, not_2_out, not_1_out, in_7);
  and and_8 (and_8_out, not_7_out, not_3_out, not_2_out, not_1_out, in_8);
endmodule

module _04 (
  input  in_1,
  input  in_2,
  input  in_3,
  input  in_4,
  input  in_5,
  input  in_6,
  output out_7
);

  wire and_1_out, and_2_out, and_3_out, and_4_out, not_1_out, not_2_out;

  not not_1 (not_1_out, in_5);
  not not_2 (not_2_out, in_6);
  and and_1 (and_1_out, in_1, in_5, in_6);
  and and_2 (and_2_out, in_2, not_1_out, in_6);
  and and_3 (and_3_out, in_3, not_2_out, in_6);
  and and_4 (and_4_out, in_4, not_1_out, not_2_out);
  or or_1 (out_7, and_1_out, and_2_out, and_3_out, and_4_out);
endmodule

module _01_lab_part_b (
  input  in_1,
  input  in_2,
  output out_3,
  output out_4,
  output out_5
);

  wire not_1_out, not_2_out, xor_1_out;

  not not_1 (not_1_out, in_2);
  xor xor_1 (xor_1_out, in_1, in_2);
  not not_2 (not_2_out, in_1);
  and and_1 (out_4, in_1, not_1_out);
  not not_3 (out_3, xor_1_out);
  and and_2 (out_5, not_2_out, in_2);
endmodule
